// Logisim project Project Decoder.circ as structural Verilog: 1 circuit, main circuit main
module main (
  input  in_1,
  input  [3:0] in_2,
  output out_3
);

  wire decoder_1_out1;

  Decoder #(.select(4)) decoder_1 (
    .out0(out_3), .out1(decoder_1_out1), .sel(in_2), .en(in_1));  // open: out2, out3, out4, out5, out6, out7, out8, out9, out10, out11, out12, out13, out14, out15
endmodule
