// Logisim project Project MUX.circ as structural Verilog: 1 circuit, main circuit main
module main (
  input  [3:0] in_1
);

  wire multiplexer_1_out, multiplexer_2_out, multiplexer_3_out, multiplexer_4_out, multiplexer_5_out,
       multiplexer_6_out, multiplexer_7_out;

  Multiplexer #(.select(4)) multiplexer_1 (
    .in0(1'b1), .in1(1'b0), .in2(1'b0), .in3(1'b0), .in4(1'b0), .in5(1'b0), .in6(1'b1), .in7(1'b1),
    .in8(1'b1), .out(multiplexer_1_out), .sel(in_1), .en(1'b1));  // open: in9, in10, in11, in12, in13, in14, in15
  Multiplexer #(.select(4)) multiplexer_2 (
    .in0(1'b1), .in1(1'b0), .in2(1'b1), .in3(1'b1), .in4(1'b0), .in5(1'b1), .in6(1'b1), .in7(1'b1),
    .in8(1'b1), .out(multiplexer_2_out), .sel(in_1), .en(1'b1));  // open: in9, in10, in11, in12, in13, in14, in15
  Multiplexer #(.select(4)) multiplexer_3 (
    .in0(1'b1), .in1(1'b1), .in2(1'b1), .in3(1'b1), .in5(1'b1), .in6(1'b1), .in7(1'b1), .in8(1'b1),
    .out(multiplexer_3_out), .sel(in_1), .en(1'b1));  // open: in4, in9, in10, in11, in12, in13, in14, in15
  Multiplexer #(.select(4)) multiplexer_4 (
    .in0(1'b0), .in1(1'b1), .in2(1'b0), .in3(1'b0), .in4(1'b0), .in5(1'b0), .in6(1'b1), .in7(1'b1),
    .in8(1'b1), .out(multiplexer_4_out), .sel(in_1), .en(1'b1));  // open: in9, in10, in11, in12, in13, in14, in15
  _7_Segment_Display u_7_segment_display_1 (
    .g(multiplexer_7_out), .f(multiplexer_6_out), .a(multiplexer_1_out), .b(multiplexer_2_out),
    .e(multiplexer_5_out), .d(multiplexer_4_out), .c(multiplexer_3_out));  // open: dp
  Multiplexer #(.select(4)) multiplexer_5 (
    .in0(1'b1), .in1(1'b1), .in2(1'b1), .in3(1'b0), .in4(1'b0), .in5(1'b0), .in6(1'b0), .in7(1'b0),
    .in8(1'b0), .out(multiplexer_5_out), .sel(in_1), .en(1'b1));  // open: in9, in10, in11, in12, in13, in14, in15
  Multiplexer #(.select(4)) multiplexer_6 (
    .in0(1'b1), .in1(1'b1), .in2(1'b1), .in3(1'b0), .in4(1'b0), .in5(1'b0), .in6(1'b1), .in7(1'b0),
    .in8(1'b1), .out(multiplexer_6_out), .sel(in_1), .en(1'b1));  // open: in9, in10, in11, in12, in13, in14, in15
  Multiplexer #(.select(4)) multiplexer_7 (
    .in0(1'b1), .in1(1'b1), .in2(1'b1), .in3(1'b0), .in4(1'b1), .in5(1'b0), .in6(1'b1), .in7(1'b1),
    .in8(1'b1), .out(multiplexer_7_out), .sel(in_1), .en(1'b1));  // open: in9, in10, in11, in12, in13, in14, in15

  // Notes on the sheet:
  //   a
  //   b
  //   c
  //   d
  //   e
  //   f
  //   g
endmodule
