// Logisim project Project NAND.circ as structural Verilog: 1 circuit, main circuit main
module main (
  input  in_1,
  input  a,
  input  b,
  input  c,
  input  d,
  output out_6,
  output out_7
);

  wire clock_1_out, nand_1_out, nand_2_out, nand_3_out, nand_4_out, nand_5_out, nand_6_out, nand_7_out,
       nand_8_out, nand_9_out, nand_10_out, nand_11_out, nand_12_out, nand_13_out, nand_14_out, nand_15_out,
       nand_16_out, nand_17_out, nand_18_out, nand_19_out, nand_20_out, nand_21_out, nand_22_out,
       nand_23_out, nand_24_out, nand_25_out, nand_26_out, nand_27_out, nand_28_out, nand_30_out,
       nand_31_out, nand_32_out, nand_33_out, nand_34_out, nand_36_out, t_ff_1_q, t_ff_2_q, t_ff_3_q,
       t_ff_4_q;

  Clock clock_1 (.out(clock_1_out));
  nand nand_1 (nand_1_out, a, a);
  T_Flip_Flop t_ff_1 (.clk(clock_1_out), .T(in_1), .Q(t_ff_1_q));  // open: Qn, preset, reset, en
  T_Flip_Flop #(.trigger("falling")) t_ff_2 (.clk(t_ff_1_q), .T(in_1), .Q(t_ff_2_q));  // open: Qn, preset, reset, en
  nand nand_2 (nand_2_out, b, b);
  T_Flip_Flop #(.trigger("falling")) t_ff_3 (.clk(t_ff_2_q), .T(in_1), .Q(t_ff_3_q));  // open: Qn, preset, reset, en
  nand nand_3 (nand_3_out, c, c);
  T_Flip_Flop #(.trigger("falling")) t_ff_4 (.clk(t_ff_3_q), .T(in_1), .Q(t_ff_4_q));  // open: Qn, preset, reset, en
  _7_Segment_Display u_7_segment_display_1 (
    .g(nand_34_out), .f(nand_21_out), .a(out_6), .b(out_7), .e(nand_33_out), .d(nand_36_out), .c(nand_24_out));  // open: dp
  nand nand_4 (nand_4_out, d, d);
  nand nand_5 (nand_5_out, b, c);
  nand nand_6 (nand_6_out, nand_2_out, nand_3_out);
  nand nand_7 (nand_7_out, nand_2_out, nand_4_out);
  nand nand_8 (nand_8_out, b, d);
  nand nand_9 (nand_9_out, b, nand_4_out);
  nand nand_10 (nand_10_out, nand_2_out, nand_3_out);
  nand nand_11 (nand_11_out, nand_1_out, nand_2_out);
  nand nand_12 (nand_12_out, nand_1_out, nand_2_out);
  nand nand_13 (nand_13_out, nand_2_out, nand_3_out);
  nand nand_14 (nand_14_out, c, nand_4_out);
  nand nand_15 (nand_15_out, nand_6_out, nand_6_out);
  nand nand_16 (nand_16_out, nand_7_out, nand_8_out);
  nand nand_17 (nand_17_out, nand_9_out, nand_9_out);
  nand nand_18 (nand_18_out, nand_10_out, nand_10_out);
  nand nand_19 (nand_19_out, nand_11_out, nand_11_out);
  nand nand_20 (nand_20_out, nand_12_out, nand_12_out);
  nand nand_21 (nand_21_out, nand_13_out, nand_14_out);
  nand nand_22 (nand_22_out, nand_13_out, d);
  nand nand_23 (nand_23_out, nand_15_out, nand_4_out);
  nand nand_24 (nand_24_out, nand_17_out, nand_3_out);
  nand nand_25 (nand_25_out, nand_18_out, d);
  nand nand_26 (nand_26_out, nand_19_out, nand_3_out);
  nand nand_27 (nand_27_out, nand_20_out, nand_4_out);
  nand nand_28 (nand_28_out, nand_22_out, nand_22_out);
  nand nand_29 (out_6, nand_5_out, nand_23_out);
  nand nand_30 (nand_30_out, nand_16_out, nand_16_out);
  nand nand_31 (nand_31_out, nand_5_out, nand_25_out);
  nand nand_32 (nand_32_out, nand_31_out, nand_31_out);
  nand nand_33 (nand_33_out, nand_26_out, nand_27_out);
  nand nand_34 (nand_34_out, nand_28_out, nand_5_out);
  nand nand_35 (out_7, nand_30_out, nand_3_out);
  nand nand_36 (nand_36_out, nand_32_out, nand_1_out);
endmodule
